# Fritzing sketch schematic (saved by Fritzing 0.9.3b)

parts:
  Part1 = Arduino Uno (Rev3)
  S1 = H-Bridge with L298N
  M1 = DC Motor
  M2 = DC Motor
  BAT1 = BC9VPC [package=bc9vpc]
  VCC1 = 4 x AAA Battery Mount
  BT1 = Bluetooth HC-06u [package=THT]

nets:
  N1: Part1.D8, S1.IN1
  N2: Part1.D9_PWM, S1.ENA
  N3: Part1.D0/RX, BT1.TXD
  N4: Part1.D1/TX, BT1.RXD
  N5: Part1.D3_PWM, S1.ENB
  N6: Part1.D4, S1.IN4
  N7: Part1.D5_PWM, S1.IN3
  N8: Part1.D7, S1.IN2
  3V3: Part1.3V3, BT1.VCC
  5V: Part1.5V, S1.5V
  GND: Part1.GND, S1.GND, BAT1.V-, BT1.GND
  N9: S1.12V, VCC1.+
  N10: S1.M1-01, M1.pin_2
  N11: S1.M1-02, M1.pin_1
  N12: S1.M2-01, M2.pin_2
  N13: S1.M2-02, M2.pin_1
  N14: BAT1.V+, VCC1.-

custom parts:
  H-Bridge with L298N: h-bridge
  Bluetooth HC-06u: Bluetooth HC-06 - face up, pins down 16.5mm x 37.5mm PCB
